# Fritzing sketch smartDevice_ (saved by Fritzing 0.9.3b)
breadboards: 1

parts:
  S1 = Pushbutton [package="[THT]"]
  LED1 = smd LED [color="Yellow (595nm)" package="1206 [SMD]"]
  Parça1 = Soil Moisture Sensor
  RHT1 = Humidity and Temperature Sensor RHT03
  U1 = NodeMCU V3.0
  R1 = Resistor [tolerance=±5% resistance=10k package="0402 [SMD]"]
  R2 = Resistor [tolerance=±5% resistance=10k package="0402 [SMD]"]
  M1 = DC Motor
  Q1 = NPN-Transistor [package="TO92 [THT]"]

nets:
  N1: S1.Pin_1, S1.Pin_2, R1.Pin_1
  VCC: S1.Pin_3, S1.Pin_4, Parça1.VCC, RHT1.Vcc, U1.D3, U1.3V3, M1.pin_2
  N2: LED1.cathode, Parça1.GND, RHT1.GND_1, U1.GND#6, U1.GND#13, U1.GND#16, U1.GND#33, R1.Pin_0, R2.Pin_0, Q1.B
  N3: Parça1.SIG, U1.A0
  N4: RHT1.Data-signal, U1.D4
  N5: U1.D1, Q1.E
  N6: U1.D2, R2.Pin_1
  N7: M1.pin_1, Q1.C

custom parts:
  NodeMCU V3.0: ESP8266 based NodeMCU
